# Fritzing sketch flame (saved by Fritzing 0.9.3b)
breadboards: 1

parts:
  U1 = NodeMCU V1.0
  Mod1 = KY-026 Flame Sensor Module [package="Breakout board"]
  LED1 = LED - 3mm [color="Red (633nm)" package="3 mm [THT]"]
  J1 = Piezo Speaker

nets:
  N1: U1.D1, Mod1.D0
  N2: U1.D2, LED1.anode
  N3: U1.D3, J1.pin1
  N4: U1.3V3, Mod1.+
  N5: U1.GND, Mod1.G, LED1.cathode, J1.pin2

custom parts:
  NodeMCU V1.0: ESP8266 based NodeMCU
  KY-026 Flame Sensor Module: KY-026 Flame Sensor Module reacts in the presence of fire.
